// Digital circuit 74LS107.dig as structural Verilog
module _74LS107 (
  input  J,
  input  CLK,
  input  K,
  input  nCLR,
  input  J_2,
  input  CLK_2,
  input  K_2,
  input  nCLR_2,
  output nQ,
  output Q,
  output nQ_2,
  output Q_2
);

  wire and_1_out, and_2_out, and_3_out, and_4_out, and_5_out, and_6_out, and_7_out, and_8_out, nand_1_out,
       nand_2_out, nand_3_out, nand_4_out;

  nor nor_1 (Q, and_2_out, and_1_out);
  nand nand_1 (nand_1_out, Q, K, CLK);
  and and_1 (and_1_out, nand_2_out, nQ);
  and and_2 (and_2_out, CLK, nQ);
  and and_3 (and_3_out, Q, nand_1_out, nCLR);
  and and_4 (and_4_out, Q, CLK, nCLR);
  nor nor_2 (nQ, and_3_out, and_4_out);
  nand nand_2 (nand_2_out, CLK, J, nQ, nCLR);
  nor nor_3 (Q_2, and_6_out, and_5_out);
  nand nand_3 (nand_3_out, Q_2, K_2, CLK_2);
  and and_5 (and_5_out, nand_4_out, nQ_2);
  and and_6 (and_6_out, CLK_2, nQ_2);
  and and_7 (and_7_out, Q_2, nand_3_out, nCLR_2);
  and and_8 (and_8_out, Q_2, CLK_2, nCLR_2);
  nor nor_4 (nQ_2, and_7_out, and_8_out);
  nand nand_4 (nand_4_out, CLK_2, J_2, nQ_2, nCLR_2);

  // Notes on the sheet:
  //   nCLR: default 1
  //   nCLR_2: default 1
endmodule
