// Digital circuit Full-Bit-Adder.dig as structural Verilog
module Full_Bit_Adder (
  input  A,
  input  B,
  input  C_in,
  output C_out,
  output SUM_out
);

  wire and_1_out, and_2_out, and_3_out, and_4_out, and_5_out, and_6_out, not_1_out, not_2_out, not_3_out,
       or_1_out, xor_1_out, xor_2_out;

  not not_1 (not_1_out, A);
  not not_2 (not_2_out, B);
  not not_3 (not_3_out, C_in);
  xor xor_1 (xor_1_out, A, B);
  and and_1 (and_1_out, not_1_out, not_2_out);
  and and_2 (and_2_out, B, A);
  and and_3 (and_3_out, xor_1_out, not_3_out);
  xor xor_2 (xor_2_out, B, C_in);
  and and_4 (and_4_out, B, C_in);
  or or_1 (or_1_out, and_1_out, and_2_out);
  and and_5 (and_5_out, or_1_out, C_in);
  and and_6 (and_6_out, A, xor_2_out);
  or or_2 (SUM_out, and_3_out, and_5_out);
  or or_3 (C_out, and_6_out, and_4_out);

  // Notes on the sheet:
  //   A XOR B
  //   ~A~B
  //   AB
  //   ~C_in(A XOR B)
  //   ~A~B + AB
  //   C_IN XOR B
  //   C_in AND B
  //   C_in(~A~B + AB)
  //   A(C_IN XOR B)
  //   SUM_out  =  ~C_in(A XOR B) + C_in(~A~B + AB)
  //   C_out =  A(C_IN XOR B) +(C_in AND B)
  //   (10 Gates for SUM_out)
  //   (4 Gates for C_out)
endmodule
