// Digital circuit Half-bit-Adder.dig as structural Verilog
module Half_bit_Adder (
  input  A,
  input  B,
  output C_out,
  output SUM_out
);

  xor xor_1 (SUM_out, A, B);
  and and_1 (C_out, B, A);

  // Notes on the sheet:
  //   A XOR B
  //   AB
endmodule
