# Fritzing sketch BCD to 7-SegDspl (saved by Fritzing 0.8.7b)
breadboards: 1

parts:
  IC1 = DIP - 16 pins [chip_label=74LS48 package="DIP (Dual Inline) [THT]"]
  SW1 = DIP SWITCH [package=dipswitch-02]
  SW2 = DIP SWITCH [package=dipswitch-02]
  DI1 = 7-Segment LED Display [package=THT]

nets:
  N1: IC1.B, SW2.1
  N2: IC1.C, SW1.2
  N3: IC1.~LT, IC1.~BI/~RBO, IC1.~RBI
  N4: IC1.D, SW1.1
  N5: IC1.A, SW2.2
  N6: IC1.e, DI1.cathodeE
  N7: IC1.d, DI1.cathodeD
  N8: IC1.c, DI1.cathodeC
  N9: IC1.b, DI1.cathodeB
  N10: IC1.a, DI1.cathodeA
  N11: IC1.g, DI1.cathodeG
  N12: IC1.f, DI1.cathodeF
  N13: IC1.VCC, SW1.3, SW1.4, SW2.3, SW2.4

custom parts:
  DIP - 16 pins: A DIP stand-in part for whatever IC you want. With 16 pins on a 300mil dual inline package (DIP) footprint.
